# Fritzing sketch Pico_DS18B20 (saved by Fritzing 0.9.10b)
breadboards: 1

parts:
  Mod1 = Raspberry Pi Pico W
  USBUART1 = CP2102 USB UART Breakout
  DS1 = DS18B20 1-Wire Temperature Sensor [part_number=DS18B20]

nets:
  N1: Mod1.pin_1, USBUART1.RXD
  N2: Mod1.pin_2, USBUART1.TXD
  GND: Mod1.pin_3, Mod1.pin_8, Mod1.pin_13, Mod1.pin_18, Mod1.pin_23, Mod1.pin_28, Mod1.pin_33, Mod1.pin_38, USBUART1.GND, DS1.GND
  N3: Mod1.pin_34, DS1.DQ
  N4: Mod1.pin_40, DS1.VDD

custom parts:
  Raspberry Pi Pico W: Raspberry Pi Pico W. Based around the RP2040 microcontroller the Pico W is a low cost microcontroller device bringing Raspberry Pi quality, cost, and easy of use to the microcontroller space. The areas marked KEEPOUT in pcb silkscreen should not have traces running through them to avoid shorts on a soldered in module!
  CP2102 USB UART Breakout: CP2102 Usb Uart Breakout Board with Battery
