# Fritzing sketch Pico_MPL3115A2 (saved by Fritzing 0.9.10b)
breadboards: 1

parts:
  Mod1 = Raspberry Pi Pico W
  Part1 = MPL3115A2 I2C Barometric Pressure, Altitude, Temperature Sensor
  USBUART1 = CP2102 USB UART Breakout

nets:
  N1: Mod1.pin_1, USBUART1.RXD
  N2: Mod1.pin_2, USBUART1.TXD
  GND: Mod1.pin_3, Mod1.pin_8, Mod1.pin_13, Mod1.pin_18, Mod1.pin_23, Mod1.pin_28, Mod1.pin_33, Mod1.pin_38, Part1.GND, USBUART1.GND
  N3: Mod1.pin_6, Part1.SDA
  N4: Mod1.pin_7, Part1.SCL
  N5: Mod1.pin_36, Part1.VIN

custom parts:
  Raspberry Pi Pico W: Raspberry Pi Pico W. Based around the RP2040 microcontroller the Pico W is a low cost microcontroller device bringing Raspberry Pi quality, cost, and easy of use to the microcontroller space. The areas marked KEEPOUT in pcb silkscreen should not have traces running through them to avoid shorts on a soldered in module!
  MPL3115A2 I2C Barometric Pressure, Altitude, Temperature Sensor: This pressure sensor from Freescale is a great low-cost sensing solution for precision measurement of barometric pressure and altitude. The MPL3115A2 has a typical 1.5 Pascal resolution, which can resolve altitude at 0.3 meters (compare to the BMP180 which can do 0.17m). It has some upsides compared to the BMP180, such as interrupt outputs for ultra-low power usage, and its also a heck of a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
  CP2102 USB UART Breakout: CP2102 Usb Uart Breakout Board with Battery
